# Fritzing sketch Alan_prot_01 (saved by Fritzing 0.9.3b)
breadboards: 3

parts:
  Componente1 = Adafruit Feather 32u4 RFM9xW LoRa [part_number="Adafruit #3078 and Adafruit #3079"]
  MUX1 = 74HC4051 [package="DIP (Dual Inline) [THT]"]  # not connected
  Q1 = Basic FET N-Channel [package="TO220 [THT]"]
  Q2 = Basic FET N-Channel [package="TO220 [THT]"]
  Q3 = Basic FET N-Channel [package="TO220 [THT]"]
  R1 = Resistor [tolerance=±5% resistance=1k package=THT]
  R2 = Resistor [tolerance=±5% resistance=1k package=THT]
  R3 = Resistor [tolerance=±5% resistance=1k package=THT]
  BATT-A = 18650 battery holder [package=battery-18650-kit]
  BATT-B = 18650 battery holder [package=battery-18650-kit]
  IC1 = SHIFT REGISTER [package=so16]
  U1 = 74HC595 [package="DIP16 [THT]"]  # not connected
  U2 = SWITCH_SPDT [package=kps-1290]
  U3 = SWITCH_SPDT [package=kps-1290]

nets:
  GND: Componente1.GND, Q1.source, IC1.GND, IC1.G
  3.3V: Componente1.+3V3, IC1.SCL, IC1.VCC
  D5: Componente1.5, IC1.SER
  D3: Componente1.3, IC1.RCK
  D2: Componente1.2, IC1.SCK
  N1: Q1.gate, R1.Pin_1
  N2: Q2.gate, R2.Pin_1
  N3: Q3.gate, R3.Pin_1
  N4: R1.Pin_0, IC1.QA
  N5: BATT-A.+, U3.P
  N6: BATT-A.-, BATT-B.-
  N7: BATT-B.+, U2.P

custom parts:
  Adafruit Feather 32u4 RFM9xW LoRa: This is the Adafruit Feather 32u4 LoRa Radio (RFM9x) - our take on an microcontroller with a "Long Range (LoRa)" packet radio transceiver with built in USB and battery charging. Its an Adafruit Feather 32u4 with a 868/915 MHz radio module cooked in! Great for making wireless networks that can go further than 2.4GHz 802.15.4 and similar, are more flexible than Bluetooth LE and without the high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
  74HC4051: 8 channel analog multiplexer/demultiplexer
  18650 battery holder: 18650 Battery Holder
